// Logisim project main.circ as structural Verilog: 8 circuits, main circuit main
module main (
  input  [4:0] RightBatY
);

  wire clock_1_out, R_out;
  wire [3:0] bit_extender_1_out, bit_extender_2_out;
  wire [4:0] joystick_1_y, kinematic_controller_1_ballx_d, kinematic_controller_1_bally_d,
       kinematic_controller_1_chipid, kinematic_controller_1_leftbaty, kinematic_controller_1_rightbaty,
       not_1_out, videochip_1_out_14, videochip_1_out_15, videochip_1_out_16, videochip_1_out_17,
       videochip_1_out_18, videochip_2_out_14, videochip_2_out_15, videochip_2_out_16, videochip_2_out_17,
       videochip_2_out_18, videochip_3_out_14, videochip_3_out_15, videochip_3_out_16, videochip_3_out_17,
       videochip_3_out_18;
  wire [7:0] scA, scB;
  wire [31:0] videochip_1_out_6, videochip_1_out_7, videochip_1_out_8, videochip_1_out_9, videochip_1_out_10,
       videochip_1_out_11, videochip_1_out_12, videochip_1_out_13, videochip_2_out_6, videochip_2_out_7,
       videochip_2_out_8, videochip_2_out_9, videochip_2_out_10, videochip_2_out_11, videochip_2_out_12,
       videochip_2_out_13, videochip_3_out_6, videochip_3_out_7, videochip_3_out_8, videochip_3_out_9,
       videochip_3_out_10, videochip_3_out_11, videochip_3_out_12, videochip_3_out_13, videochip_4_out_6,
       videochip_4_out_7, videochip_4_out_8, videochip_4_out_9, videochip_4_out_10, videochip_4_out_11,
       videochip_4_out_12, videochip_4_out_13;

  // CdM_8_mark5 cdm_8_mark5_1: pin names not known
  Hex_Digit_Display hex_digit_display_1 (.value(bit_extender_1_out));  // open: dp
  Hex_Digit_Display hex_digit_display_2 (.value(bit_extender_1_out));  // open: dp
  Bit_Extender #(.out_width(4)) bit_extender_1 (.in(scA), .out(bit_extender_1_out));
  Joystick #(.bits(5)) joystick_1 (.y(joystick_1_y));  // open: x
  assign not_1_out = ~joystick_1_y;  // NOT_Gate not_1, 5 bits wide
  Button R (.out(R_out));
  Videochip videochip_1 (
    .BallX(kinematic_controller_1_ballx_d), .BallY(kinematic_controller_1_bally_d),
    .LeftBatY(kinematic_controller_1_leftbaty), .RightBatY(kinematic_controller_1_rightbaty),
    .ChipID(kinematic_controller_1_chipid), .out_18(videochip_1_out_18), .out_14(videochip_1_out_14),
    .out_15(videochip_1_out_15), .out_16(videochip_1_out_16), .out_17(videochip_1_out_17),
    .out_6(videochip_1_out_6), .out_8(videochip_1_out_8), .out_9(videochip_1_out_9),
    .out_10(videochip_1_out_10), .out_11(videochip_1_out_11), .out_12(videochip_1_out_12),
    .out_13(videochip_1_out_13), .out_7(videochip_1_out_7));
  DotMatrix #(.matrixcols(32), .matrixrows(32)) dotmatrix_1 (
    .col0(videochip_1_out_6), .col1(videochip_1_out_7), .col2(videochip_1_out_8), .col3(videochip_1_out_9),
    .col4(videochip_1_out_10), .col5(videochip_1_out_11), .col6(videochip_1_out_12),
    .col7(videochip_1_out_13), .col8(videochip_2_out_6), .col9(videochip_2_out_7), .col10(videochip_2_out_8),
    .col11(videochip_2_out_9), .col12(videochip_2_out_10), .col13(videochip_2_out_11),
    .col14(videochip_2_out_12), .col15(videochip_2_out_13), .col16(videochip_3_out_6),
    .col17(videochip_3_out_7), .col18(videochip_3_out_8), .col19(videochip_3_out_9),
    .col20(videochip_3_out_10), .col21(videochip_3_out_11), .col22(videochip_3_out_12),
    .col23(videochip_3_out_13), .col24(videochip_4_out_6), .col25(videochip_4_out_7),
    .col26(videochip_4_out_8), .col27(videochip_4_out_9), .col28(videochip_4_out_10),
    .col29(videochip_4_out_11), .col30(videochip_4_out_12), .col31(videochip_4_out_13));
  Kinematic_Controller kinematic_controller_1 (
    .RightYIn(RightBatY), .BallX_D(kinematic_controller_1_ballx_d), .BallY_D(kinematic_controller_1_bally_d),
    .LeftBatY(kinematic_controller_1_leftbaty), .RightBatY(kinematic_controller_1_rightbaty),
    .ChipID(kinematic_controller_1_chipid), .Reset(R_out), .LeftYIn(not_1_out), .scoreA(scA),
    .Clock(clock_1_out), .scoreB(scB));  // open: BallX_8, BallY_8, vxy
  Clock clock_1 (.out(clock_1_out));
  Videochip videochip_2 (
    .BallX(videochip_1_out_14), .BallY(videochip_1_out_15), .LeftBatY(videochip_1_out_16),
    .RightBatY(videochip_1_out_17), .ChipID(videochip_1_out_18), .out_18(videochip_2_out_18),
    .out_14(videochip_2_out_14), .out_15(videochip_2_out_15), .out_16(videochip_2_out_16),
    .out_17(videochip_2_out_17), .out_6(videochip_2_out_6), .out_8(videochip_2_out_8),
    .out_9(videochip_2_out_9), .out_10(videochip_2_out_10), .out_11(videochip_2_out_11),
    .out_12(videochip_2_out_12), .out_13(videochip_2_out_13), .out_7(videochip_2_out_7));
  Videochip videochip_3 (
    .BallX(videochip_2_out_14), .BallY(videochip_2_out_15), .LeftBatY(videochip_2_out_16),
    .RightBatY(videochip_2_out_17), .ChipID(videochip_2_out_18), .out_18(videochip_3_out_18),
    .out_14(videochip_3_out_14), .out_15(videochip_3_out_15), .out_16(videochip_3_out_16),
    .out_17(videochip_3_out_17), .out_6(videochip_3_out_6), .out_8(videochip_3_out_8),
    .out_9(videochip_3_out_9), .out_10(videochip_3_out_10), .out_11(videochip_3_out_11),
    .out_12(videochip_3_out_12), .out_13(videochip_3_out_13), .out_7(videochip_3_out_7));
  Videochip videochip_4 (
    .BallX(videochip_3_out_14), .BallY(videochip_3_out_15), .LeftBatY(videochip_3_out_16),
    .RightBatY(videochip_3_out_17), .ChipID(videochip_3_out_18), .out_6(videochip_4_out_6),
    .out_8(videochip_4_out_8), .out_9(videochip_4_out_9), .out_10(videochip_4_out_10),
    .out_11(videochip_4_out_11), .out_12(videochip_4_out_12), .out_13(videochip_4_out_13),
    .out_7(videochip_4_out_7));  // open: out_18, out_14, out_15, out_16, out_17
  Hex_Digit_Display hex_digit_display_3 (.value(bit_extender_2_out));  // open: dp
  Hex_Digit_Display hex_digit_display_4 (.value(bit_extender_2_out));  // open: dp
  Bit_Extender #(.out_width(4)) bit_extender_2 (.in(scB), .out(bit_extender_2_out));

  // Notes on the sheet:
  //   Менің Бағдарламам
endmodule

module Videochip (
  input  [4:0] BallX,
  input  [4:0] BallY,
  input  [4:0] LeftBatY,
  input  [4:0] RightBatY,
  input  [4:0] ChipID,
  output [31:0] out_6,
  output [31:0] out_7,
  output [31:0] out_8,
  output [31:0] out_9,
  output [31:0] out_10,
  output [31:0] out_11,
  output [31:0] out_12,
  output [31:0] out_13,
  output [4:0] out_14,
  output [4:0] out_15,
  output [4:0] out_16,
  output [4:0] out_17,
  output [4:0] out_18
);

  wire [31:0] ball_4_out_5, ball_5_out_5, bat_1_out_5, bat_2_out_5;

  Ball ball_1 (.BallX(BallX), .BallY(BallY), .NumColumn({5{1'b0}}), .ChipID(ChipID), .out_5(out_6));
  Ball ball_2 (.BallX(BallX), .BallY(BallY), .NumColumn(5'b00001), .ChipID(ChipID), .out_5(out_7));
  Ball ball_3 (.BallX(BallX), .BallY(BallY), .NumColumn(5'b00010), .ChipID(ChipID), .out_5(out_8));
  assign out_9 = bat_1_out_5 | ball_4_out_5;  // OR_Gate or_1, 32 bits wide
  Bat bat_1 (.BatX(5'b00011), .BatY(LeftBatY), .NumColumn(5'b00011), .ChipID(ChipID), .out_5(bat_1_out_5));
  Ball ball_4 (.BallX(BallX), .BallY(BallY), .NumColumn(5'b00011), .ChipID(ChipID), .out_5(ball_4_out_5));
  Adder #(.width(5)) adder_1 (.a(ChipID), .b(5'b00001), .out(out_18));  // open: cin, cout
  assign out_10 = bat_2_out_5 | ball_5_out_5;  // OR_Gate or_2, 32 bits wide
  Bat bat_2 (.BatX(5'b11100), .BatY(RightBatY), .NumColumn(5'b00100), .ChipID(ChipID), .out_5(bat_2_out_5));
  Ball ball_5 (.BallX(BallX), .BallY(BallY), .NumColumn(5'b00100), .ChipID(ChipID), .out_5(ball_5_out_5));
  Ball ball_6 (.BallX(BallX), .BallY(BallY), .NumColumn(5'b00101), .ChipID(ChipID), .out_5(out_11));
  Ball ball_7 (.BallX(BallX), .BallY(BallY), .NumColumn(5'b00110), .ChipID(ChipID), .out_5(out_12));
  Ball ball_8 (.BallX(BallX), .BallY(BallY), .NumColumn(5'b00111), .ChipID(ChipID), .out_5(out_13));

  assign out_14 = BallX;
  assign out_15 = BallY;
  assign out_16 = LeftBatY;
  assign out_17 = RightBatY;
endmodule

module Bat (
  input  [4:0] BatX,
  input  [4:0] BatY,
  input  [4:0] NumColumn,
  input  [4:0] ChipID,
  output [31:0] out_5
);

  wire comparator_1_eq;
  wire [4:0] adder_1_out, multiplier_1_out;
  wire [31:0] decoder_1_out0, or_1_out, shifter_1_out, shifter_2_out;

  Decoder #(.select(5), .disabled(0)) decoder_1 (
    .out0(decoder_1_out0[0]), .out1(decoder_1_out0[1]), .out2(decoder_1_out0[2]), .out3(decoder_1_out0[3]),
    .out4(decoder_1_out0[4]), .out5(decoder_1_out0[5]), .out6(decoder_1_out0[6]), .out7(decoder_1_out0[7]),
    .out8(decoder_1_out0[8]), .out9(decoder_1_out0[9]), .out10(decoder_1_out0[10]),
    .out11(decoder_1_out0[11]), .out12(decoder_1_out0[12]), .out13(decoder_1_out0[13]),
    .out14(decoder_1_out0[14]), .out15(decoder_1_out0[15]), .out16(decoder_1_out0[16]),
    .out17(decoder_1_out0[17]), .out18(decoder_1_out0[18]), .out19(decoder_1_out0[19]),
    .out20(decoder_1_out0[20]), .out21(decoder_1_out0[21]), .out22(decoder_1_out0[22]),
    .out23(decoder_1_out0[23]), .out24(decoder_1_out0[24]), .out25(decoder_1_out0[25]),
    .out26(decoder_1_out0[26]), .out27(decoder_1_out0[27]), .out28(decoder_1_out0[28]),
    .out29(decoder_1_out0[29]), .out30(decoder_1_out0[30]), .out31(decoder_1_out0[31]), .sel(BatY));  // open: en
  Multiplier #(.width(5)) multiplier_1 (.a(ChipID), .b(5'b01000), .out(multiplier_1_out));  // open: cin, cout
  Shifter #(.width(32)) shifter_1 (.in(decoder_1_out0), .\dist (5'b00001), .out(shifter_1_out));
  Shifter #(.width(32)) shifter_2 (.in(decoder_1_out0), .\dist (5'b00010), .out(shifter_2_out));
  Adder #(.width(5)) adder_1 (.a(NumColumn), .b(multiplier_1_out), .out(adder_1_out));  // open: cin, cout
  assign or_1_out = shifter_1_out | decoder_1_out0 | shifter_2_out;  // OR_Gate or_1, 32 bits wide
  Comparator #(.width(5), .mode("unsigned")) comparator_1 (
    .a(BatX), .b(adder_1_out), .eq(comparator_1_eq));  // open: gt, lt
  Multiplexer #(.width(32), .disabled(0), .enable("false")) multiplexer_1 (
    .in0({32{1'b0}}), .in1(or_1_out), .out(out_5), .sel(comparator_1_eq));
endmodule

module Ball (
  input  [4:0] BallX,
  input  [4:0] BallY,
  input  [4:0] NumColumn,
  input  [4:0] ChipID,
  output [31:0] out_5
);

  wire comparator_1_eq;
  wire [4:0] adder_1_out, multiplier_1_out;
  wire [31:0] decoder_1_out0;

  Decoder #(.select(5), .disabled(0)) decoder_1 (
    .out0(decoder_1_out0[0]), .out1(decoder_1_out0[1]), .out2(decoder_1_out0[2]), .out3(decoder_1_out0[3]),
    .out4(decoder_1_out0[4]), .out5(decoder_1_out0[5]), .out6(decoder_1_out0[6]), .out7(decoder_1_out0[7]),
    .out8(decoder_1_out0[8]), .out9(decoder_1_out0[9]), .out10(decoder_1_out0[10]),
    .out11(decoder_1_out0[11]), .out12(decoder_1_out0[12]), .out13(decoder_1_out0[13]),
    .out14(decoder_1_out0[14]), .out15(decoder_1_out0[15]), .out16(decoder_1_out0[16]),
    .out17(decoder_1_out0[17]), .out18(decoder_1_out0[18]), .out19(decoder_1_out0[19]),
    .out20(decoder_1_out0[20]), .out21(decoder_1_out0[21]), .out22(decoder_1_out0[22]),
    .out23(decoder_1_out0[23]), .out24(decoder_1_out0[24]), .out25(decoder_1_out0[25]),
    .out26(decoder_1_out0[26]), .out27(decoder_1_out0[27]), .out28(decoder_1_out0[28]),
    .out29(decoder_1_out0[29]), .out30(decoder_1_out0[30]), .out31(decoder_1_out0[31]), .sel(BallY));  // open: en
  Multiplier #(.width(5)) multiplier_1 (.a(ChipID), .b(5'b01000), .out(multiplier_1_out));  // open: cin, cout
  Adder #(.width(5)) adder_1 (.a(NumColumn), .b(multiplier_1_out), .out(adder_1_out));  // open: cin, cout
  Comparator #(.width(5), .mode("unsigned")) comparator_1 (
    .a(BallX), .b(adder_1_out), .eq(comparator_1_eq));  // open: gt, lt
  Multiplexer #(.width(32), .disabled(0), .enable("false")) multiplexer_1 (
    .in0({32{1'b0}}), .in1(decoder_1_out0), .out(out_5), .sel(comparator_1_eq));
endmodule

module Kinematic_Controller (
  input  Reset,
  input  [4:0] LeftYIn,
  input  [4:0] RightYIn,
  input  Clock,
  output [7:0] BallX_8,
  output [4:0] BallX_D,
  output [4:0] BallY_D,
  output [7:0] BallY_8,
  output [4:0] LeftBatY,
  output [4:0] RightBatY,
  output [7:0] vxy,
  output [4:0] ChipID,
  output [7:0] scoreA,
  output [7:0] scoreB
);

  wire adder_5_cout, adder_6_cout, adder_9_cout, adder_10_cout, and_1_out, Bcontact, comparator_1_eq,
       comparator_2_eq, comparator_3_eq, comparator_4_eq, hitA, hitB, inrange_1_sharearow,
       inrange_2_sharearow, LBcontact, not_1_out, not_2_out, not_3_out, not_4_out, not_5_out, not_6_out,
       not_9_out, not_10_out, or_2_out, or_3_out, or_4_out, or_5_out, RBcontact, reset_t, xrefl, yrefl;
  wire [2:0] multiplexer_3_out, multiplexer_4_out, reflect_1_newv, reflect_2_newv;
  wire [7:0] adder_1_out, adder_2_out, adder_3_out, adder_4_out, adder_7_out, adder_8_out, longVX, longVY,
       multiplexer_1_out, multiplexer_2_out, multiplexer_5_out, multiplexer_6_out;

  or or_1 (reset_t, hitB, Reset);
  not not_1 (not_1_out, xrefl);
  not not_2 (not_2_out, Bcontact);
  Adder adder_1 (.a(BallX_8), .b(longVX), .out(adder_1_out));  // open: cin, cout
  and and_1 (and_1_out, not_1_out, not_2_out);
  or or_2 (or_2_out, and_1_out, Reset);
  Adder adder_2 (.a(BallY_8), .b(longVY), .out(adder_2_out));  // open: cin, cout
  not not_3 (not_3_out, yrefl);
  or or_3 (or_3_out, not_3_out, Reset);
  Register register_1 (.D(multiplexer_1_out), .en(or_2_out), .Q(BallX_8), .clk(not_4_out));  // open: clr
  Multiplexer #(.width(8), .disabled(0), .enable("false")) multiplexer_1 (
    .in0(adder_1_out), .in1(8'hc0), .out(multiplexer_1_out), .sel(reset_t));
  not not_4 (not_4_out, Clock);
  Multiplexer #(.width(8), .disabled(0), .enable("false")) multiplexer_2 (
    .in0(adder_2_out), .in1(8'h80), .out(multiplexer_2_out), .sel(reset_t));
  Register register_2 (.D(multiplexer_2_out), .en(or_3_out), .Q(BallY_8), .clk(not_5_out));  // open: clr
  not not_5 (not_5_out, Clock);
  // Probe on vxy[2:0]
  newVX newvx_1 (.v(vxy[2:0]), .longV(longVX));
  // Probe on vxy[5:3]
  newVX newvx_2 (.v(vxy[5:3]), .longV(longVY));
  reflect reflect_1 (.newv(reflect_1_newv), .oldv(vxy[2:0]));
  Multiplexer #(.width(3), .disabled(0), .enable("false")) multiplexer_3 (
    .in0(reflect_1_newv), .in1(3'b100), .out(multiplexer_3_out), .sel(reset_t));
  or or_4 (or_4_out, xrefl, Bcontact, Reset);
  reflect reflect_2 (.newv(reflect_2_newv), .oldv(vxy[5:3]));
  Multiplexer #(.width(3), .disabled(0), .enable("false")) multiplexer_4 (
    .in0(reflect_2_newv), .in1(3'b011), .out(multiplexer_4_out), .sel(reset_t));
  or or_5 (or_5_out, yrefl, Reset);
  Adder adder_3 (.a(8'h1), .b(scoreA), .out(adder_3_out));  // open: cin, cout
  Adder adder_4 (.a(8'h1), .b(scoreB), .out(adder_4_out));  // open: cin, cout
  Multiplexer #(.width(8), .disabled(0), .enable("false")) multiplexer_5 (
    .in0(8'h6), .in1(8'hfc), .out(multiplexer_5_out), .sel(longVX[7]));
  Multiplexer #(.width(8), .disabled(0), .enable("false")) multiplexer_6 (
    .in0(8'h6), .in1(8'hfc), .out(multiplexer_6_out), .sel(longVY[7]));
  not not_6 (not_6_out, longVX[7]);
  Register #(.width(3)) register_3 (.D(multiplexer_3_out), .en(or_4_out), .Q(vxy[2:0]), .clk(Clock));  // open: clr
  Register #(.width(3)) register_4 (.D(multiplexer_4_out), .en(or_5_out), .Q(vxy[5:3]), .clk(Clock));  // open: clr
  Register register_5 (.D(adder_3_out), .en(hitA), .Q(scoreA), .clk(Clock), .clr(Reset));
  Register register_6 (.D(adder_4_out), .en(hitB), .Q(scoreB), .clk(Clock), .clr(Reset));
  Adder adder_5 (.a(BallX_8), .b(multiplexer_5_out), .cout(adder_5_cout));  // open: out, cin
  Adder adder_6 (.a(BallY_8), .b(multiplexer_6_out), .cout(adder_6_cout));  // open: out, cin
  and and_2 (hitA, xrefl, longVX[7]);
  and and_3 (hitB, xrefl, not_6_out);
  Comparator #(.width(1), .mode("unsigned")) comparator_1 (
    .a(longVX[7]), .b(adder_5_cout), .eq(comparator_1_eq));  // open: gt, lt
  not not_7 (xrefl, comparator_1_eq);
  not not_8 (yrefl, comparator_2_eq);
  Comparator #(.width(1), .mode("unsigned")) comparator_2 (
    .a(longVY[7]), .b(adder_6_cout), .eq(comparator_2_eq));  // open: gt, lt
  Adder adder_7 (.a(BallX_8), .b(8'he4), .out(adder_7_out));  // open: cin, cout
  Adder adder_8 (.a(BallX_8), .b(8'h1c), .out(adder_8_out));  // open: cin, cout
  Adder adder_9 (.a(adder_7_out), .b(longVX), .cout(adder_9_cout));  // open: out, cin
  Adder adder_10 (.a(adder_8_out), .b(longVX), .cout(adder_10_cout));  // open: out, cin
  Comparator #(.width(1), .mode("unsigned")) comparator_3 (
    .a(adder_9_cout), .b(longVX[7]), .eq(comparator_3_eq));  // open: gt, lt
  Comparator #(.width(1), .mode("unsigned")) comparator_4 (
    .a(adder_10_cout), .b(longVX[7]), .eq(comparator_4_eq));  // open: gt, lt
  not not_9 (not_9_out, comparator_3_eq);
  inrange inrange_1 (.YBall(BallY_8[7:3]), .YBat(LeftYIn), .shareArow(inrange_1_sharearow));
  not not_10 (not_10_out, comparator_4_eq);
  inrange inrange_2 (.YBall(BallY_8[7:3]), .YBat(RightYIn), .shareArow(inrange_2_sharearow));
  and and_4 (LBcontact, not_9_out, inrange_1_sharearow);
  and and_5 (RBcontact, not_10_out, inrange_2_sharearow);
  or or_6 (Bcontact, LBcontact, RBcontact);

  assign BallX_D = BallX_8[7:3];
  assign BallY_D = BallY_8[7:3];
  assign ChipID = {5{1'b0}};
  assign LeftBatY = LeftYIn;
  assign RightBatY = RightYIn;
  assign vxy[7:6] = 2'b00;

  // Other names for the same wires on the sheet: vxneg = longVX[7]; vyneg = longVY[7]; R = Reset; scA[7:0] = scoreA;
  //   scB[7:0] = scoreB; vx[2:0] = vxy[2:0]; vy[2:0] = vxy[5:3]; x[4:0] = BallX_8[7:3]; xreg[7:0] = BallX_8;
  //   y[4:0] = BallY_8[7:3]; yreg[7:0] = BallY_8

  // Notes on the sheet:
  //   CDM-8'ту же это надо?
  //   ON FALLING EDGE OF CLOCK
  //   ON RISING EDGE OF CLOCK
endmodule

module reflect (
  input  [2:0] oldv,
  output [2:0] newv
);

  wire comparator_1_eq;
  wire [2:0] adder_1_out, not_1_out;

  assign not_1_out = ~oldv;  // NOT_Gate not_1, 3 bits wide
  Comparator #(.width(3), .mode("unsigned")) comparator_1 (.a(oldv), .b(3'b100), .eq(comparator_1_eq));  // open: gt, lt
  Adder #(.width(3)) adder_1 (.a(not_1_out), .b(3'b001), .out(adder_1_out));  // open: cin, cout
  Multiplexer #(.width(3), .disabled(0), .enable("false")) multiplexer_1 (
    .in0(adder_1_out), .in1(not_1_out), .out(newv), .sel(comparator_1_eq));
endmodule

module inrange (
  input  [4:0] YBall,
  input  [4:0] YBat,
  output shareArow
);

  wire comparator_1_eq, comparator_2_eq, comparator_3_eq;
  wire [4:0] adder_1_out, adder_2_out;

  Adder #(.width(5)) adder_1 (.a(YBat), .b(5'b00001), .out(adder_1_out));  // open: cin, cout
  Adder #(.width(5)) adder_2 (.a(adder_1_out), .b(5'b00001), .out(adder_2_out));  // open: cin, cout
  Comparator #(.width(5), .mode("unsigned")) comparator_1 (.a(YBat), .b(YBall), .eq(comparator_1_eq));  // open: gt, lt
  Comparator #(.width(5), .mode("unsigned")) comparator_2 (
    .a(adder_1_out), .b(YBall), .eq(comparator_2_eq));  // open: gt, lt
  Comparator #(.width(5), .mode("unsigned")) comparator_3 (
    .a(adder_2_out), .b(YBall), .eq(comparator_3_eq));  // open: gt, lt
  or or_1 (shareArow, comparator_1_eq, comparator_2_eq, comparator_3_eq);
endmodule

module newVX (
  input  [2:0] v,
  output [7:0] longV
);

  // Probe on v
  // Probe on {{6{v[2]}}, v[1:0]}

  assign longV = {{6{v[2]}}, v[1:0]};
endmodule
